# Fritzing sketch TrimrAnalogBlink (saved by Fritzing 0.9.1b)
breadboards: 2

parts:
  Part1 = Arduino Uno (Rev3)
  R1 = Trimmer Potentiometer [maximum_resistance=10kΩ package=THT]
  LED1 = LED - 5mm [color="Red (633nm)" package="5 mm [THT]"]

nets:
  N1: Part1.A0, R1.wiper
  N2: Part1.D13/SCK, LED1.anode
  N3: Part1.GND, R1.leg1, LED1.cathode
  N4: Part1.5V, R1.leg2

// code stored in the sketch: Untitled.ino
const int analogPin = A0;
const int LED = 13;
int hodnota = 0;


void setup() {
  Serial.begin(9600); 
  pinMode(LED, OUTPUT);
}

void loop() {

  hodnota = analogRead(analogPin);
  Serial.print("hodnota = " );
  Serial.print(hodnota); 
  Serial.println();
  digitalWrite(LED, HIGH);
  delay(hodnota);
  digitalWrite(LED, LOW);  
  delay(hodnota);
}
