# Fritzing sketch lcdtrimr (saved by Fritzing 0.9.1b)
breadboards: 1

parts:
  Part1 = Arduino Uno (Rev3)
  R1 = Trimmer Potentiometer [maximum_resistance=10kΩ package=THT]
  U1 = LCD-16X2 [package=lcd-16x2]

nets:
  N1: Part1.A0, R1.wiper
  N2: Part1.D2, U1.RS
  N3: Part1.D3_PWM, U1.E
  N4: Part1.D4, U1.DB4
  N5: Part1.D5_PWM, U1.DB5
  N6: Part1.D6_PWM, U1.DB6
  N7: Part1.D7, U1.DB7
  5V: Part1.5V, R1.leg2, U1.VDD, U1.A
  GND: Part1.GND, R1.leg1, U1.VSS, U1.VO, U1.R_W, U1.K

// code stored in the sketch: lcdtrimr.ino
#include <LiquidCrystal.h>

LiquidCrystal MojeLCD1(2,3,4,5,6,7);

const int analogPin = A0;
int hodnota = 0;


void setup() {
  Serial.begin(9600); 
  MojeLCD1.begin(20, 4);
  MojeLCD1.print("Cteni hodnoty z A0");
}

void loop() {

  hodnota = analogRead(analogPin);
  Serial.print("hodnota = " );
  Serial.print(hodnota); 
  Serial.println();
  
  MojeLCD1.setCursor(0,3);
  MojeLCD1.print("hodnota = ");
  MojeLCD1.print(hodnota);
  MojeLCD1.print(" ");
  
  delay(100);
  
}
