# Fritzing sketch sketch (saved by Fritzing 0.9.2b)
circuit board: 8.46667cm x 5.64444cm
breadboards: 1

parts:
  PIR1 = PIR sensor
  U1 = attiny85 [package=dip]
  LED1 = LED - 5mm [color="Red (633nm)" package="5 mm [THT]"]
  J1 = Piezo Speaker
  R1 = Resistor [tolerance=±5% resistance=220 package=THT]
  R2 = Resistor [tolerance=±5% resistance=220 package=THT]
  U2 = RELAY [package=relay-g5q]

nets:
  N1: PIR1.VDD, U1.Pin_8
  N2: PIR1.SIG, U1.Pin_2
  N3: PIR1.GND, U1.Pin_4, LED1.cathode, J1.pin1, U2.COIL2
  N4: U1.Pin_3, U2.COIL1
  N5: U1.Pin_5, R2.Pin_0
  N6: U1.Pin_6, R1.Pin_0
  N7: LED1.anode, R1.Pin_1
  N8: J1.pin2, R2.Pin_1

// code stored in the sketch: KuchynMamkaFritzing.ino
/* 
 * //////////////////////////////////////////////////
 * //making sense of the Parallax PIR sensor's output
 * //////////////////////////////////////////////////
 *
 * Switches a LED according to the state of the sensors output pin.
 * Determines the beginning and end of continuous motion sequences.
 *
 * @author: Kristian Gohlke / krigoo (_) gmail (_) com / http://krx.at
 * @date:   3. September 2006 
 *
 * kr1 (cleft) 2006 
 * released under a creative commons "Attribution-NonCommercial-ShareAlike 2.0" license
 * http://creativecommons.org/licenses/by-nc-sa/2.0/de/
 *
 *
 * The Parallax PIR Sensor is an easy to use digital infrared motion sensor module. 
 * (http://www.parallax.com/detail.asp?product_id=555-28027)
 *
 * The sensor's output pin goes to HIGH if motion is present.
 * However, even if motion is present it goes to LOW from time to time, 
 * which might give the impression no motion is present. 
 * This program deals with this issue by ignoring LOW-phases shorter than a given time, 
 * assuming continuous motion is present during these phases.
 *  
 */

/////////////////////////////
//VARS

//the time when the sensor outputs a low impulse
long unsigned int lowIn;         

//the amount of milliseconds the sensor has to be low 
//before we assume all motion has stopped
long unsigned int pause = 30000;  

boolean lockLow = true;
boolean takeLowTime;  

int pirPin = 8;    //the digital pin connected to the PIR sensor's output
int ledPin = 13;
int relay = 12;
int buzz = 11;
int x = 0;


/////////////////////////////
//SETUP
void setup(){
  Serial.begin(9600);
  pinMode(pirPin, INPUT);
  pinMode(ledPin, OUTPUT);
  pinMode(relay, OUTPUT);
  pinMode(buzz, OUTPUT);
  digitalWrite(pirPin, LOW);
  digitalWrite(relay, LOW);
  digitalWrite(buzz, LOW);

  do
  {
    digitalWrite(ledPin, HIGH);
    delay(50);
    digitalWrite(ledPin, LOW);
    delay(50);
    x++;
  
  } while (x < 3);
}

////////////////////////////
//LOOP
void loop(){

     if(digitalRead(pirPin) == HIGH){
       digitalWrite(ledPin, HIGH);   //the led visualizes the sensors output pin state
       digitalWrite(relay, HIGH);
       if(lockLow){  
         //makes sure we wait for a transition to LOW before any further output is made:
         lockLow = false;            
         Serial.println("---");
         Serial.print("motion detected at ");
         Serial.print(millis()/1000);
         Serial.println(" sec"); 
         delay(50);
         }         
         takeLowTime = true;
       }

     if(digitalRead(pirPin) == LOW){       
       digitalWrite(ledPin, LOW);  //the led visualizes the sensors output pin state

       if(takeLowTime){
        lowIn = millis();          //save the time of the transition from high to LOW
        takeLowTime = false;       //make sure this is only done at the start of a LOW phase
        }
       //if the sensor is low for more than the given pause, 
       //we assume that no more motion is going to happen
       if(!lockLow && millis() - lowIn > pause){  
           //makes sure this block of code is only executed again after 
           //a new motion sequence has been detected
           lockLow = true;                        
           Serial.print("motion ended at ");      //output
           Serial.print((millis() - pause)/1000);
           Serial.println(" sec");
           digitalWrite(buzz, HIGH);
           delay(50);
           digitalWrite(buzz, LOW);
           }
       }

    if ( lockLow == true && digitalRead(pirPin) == LOW ) {
      delay(10000);
      digitalWrite(relay, LOW);  
    }
  }
