# Fritzing sketch sketch (saved by Fritzing 0.9.2b)
breadboards: 1

parts:
  Part1 = Arduino Pro Mini v13
  Part2 = Arduino GSM Shield
  Grove1 = Grove OLED 128x96

nets:
  VCC: Part1.VCC, Grove1.VCC
  GND: Part1.GND, Part2.AGND, Grove1.GND
  N1: Part1.A2, Grove1.SDA
  N2: Part1.A1, Grove1.SCL
  N3: Part1.D8, Part2.DSM_RX_D2
  N4: Part1.D7, Part2.DSM_TX_D3
