# Fritzing sketch shiftRegistr (saved by Fritzing 0.9.1b)
breadboards: 2

parts:
  Part1 = Arduino Uno (Rev3) - ICSP
  U1 = 74HC595 SMD [package="SO16 [SMD]"]
  LED1 = LED - 5mm [color="Red (633nm)" package="5 mm [THT]"]
  LED2 = LED - 5mm [color="Red (633nm)" package="5 mm [THT]"]
  LED3 = LED - 5mm [color="Red (633nm)" package="5 mm [THT]"]
  LED4 = LED - 5mm [color="Red (633nm)" package="5 mm [THT]"]
  LED5 = LED - 5mm [color="Red (633nm)" package="5 mm [THT]"]
  LED6 = LED - 5mm [color="Red (633nm)" package="5 mm [THT]"]
  LED7 = LED - 5mm [color="Red (633nm)" package="5 mm [THT]"]
  LED8 = LED - 5mm [color="Red (633nm)" package="5 mm [THT]"]

nets:
  GND: Part1.GND, U1.GND, U1.OE, LED1.cathode, LED2.cathode, LED3.cathode, LED4.cathode, LED5.cathode, LED6.cathode, LED7.cathode, LED8.cathode
  5V: Part1.5V, U1.MR, U1.VCC
  N1: Part1.D8, U1.DS
  N2: Part1.D9_PWM, U1.ST_CP
  N3: Part1.D10_PWM/SS, U1.SH_CP
  N4: U1.Q1, LED2.anode
  N5: U1.Q2, LED3.anode
  N6: U1.Q3, LED4.anode
  N7: U1.Q4, LED5.anode
  N8: U1.Q5, LED6.anode
  N9: U1.Q6, LED7.anode
  N10: U1.Q7, LED8.anode
  N11: U1.Q0, LED1.anode

// code stored in the sketch: shiftRegistr.ino
// pin p?ipojen na RCLK registru (12)
int latchPin = 9;
//Pin connected to SRCLK registru (11)
int clockPin = 10;
////Pin p?ipojen na Data pin registu (14)
int dataPin = 8;

 
// data ulo?ená v poli
// v binární soustav? pro v?t?í
// p?ehlednost
byte data[] =
  {
  B10000000,
  B01000000,
  B00100000,
  B00010000,
  B00001000,
  B00000100,
  B00000010,
  B00000001,
  B00000010,
  B00000100,
  B00001000,
  B00010000,
  B00100000,
  B01000000
  };
 
 
void setup() {
  // nastaví na?e piny pro regist na výstupní
  pinMode(latchPin, OUTPUT);
  pinMode(clockPin, OUTPUT);
  pinMode(dataPin, OUTPUT);
}
 
void loop() {
  // funkce projde v?echny byte v poli data
  for (int index = 0; index < sizeof(data); index++) {
    // kdy? dáme latchPin na LOW mu?eme
    // do registru poslat data
    digitalWrite(latchPin, LOW);
    // a to pomocí funkce shiftOut, která
    shiftOut(dataPin, clockPin, MSBFIRST, data[index]);  
 
    // jakmile dále latchPin na HIGH,
    // data se objeví na výstupu
    digitalWrite(latchPin, HIGH);
   
    // po?ká 50ms, aby jsme výsledek vid?li
    delay(30);
  }
 
  }
